# Fritzing sketch PIRRGBledUNO12V (saved by Fritzing 0.9.2b)
breadboards: 1

parts:
  RGB_led = RGB LED - (4 legs) [package="5 mm [THT]"]
  Part3 = Arduino Uno (Rev3) - ICSP
  part = Resistor [tolerance=±5% resistance=330 package=THT]
  part_2 = Resistor [tolerance=±5% resistance=330 package=THT]
  part_3 = Resistor [tolerance=±5% resistance=330 package=THT]
  PIR2 = PIR sensor
  R4 = Resistor [tolerance=±5% resistance=10k package="1206 [SMD]"]
  12V = Power plug

nets:
  N1: RGB_led.red_cathode, part_3.Pin_0
  5V: RGB_led.common_anode, Part3.5V, PIR2.VCC, R4.Pin_1
  N2: RGB_led.green_cathode, part_2.Pin_0
  N3: RGB_led.blue_cathode, part.Pin_0
  N4: Part3.D10_PWM/SS, PIR2.SIG, R4.Pin_0
  N5: Part3.D3_PWM, part.Pin_1
  N6: Part3.D5_PWM, part_2.Pin_1
  N7: Part3.D6_PWM, part_3.Pin_1
  GND: Part3.GND, PIR2.GND, 12V.GND
  VIN: Part3.VIN, 12V.VCC
